# Fritzing sketch RPi-PwmFan-fritz (saved by Fritzing 0.9.3b)
breadboards: 1

parts:
  Raspberry_Pi_1 = Raspberry Pi 3 [part_number=RPI-3-V1.2]
  Power_plug1 = Power plug
  H1 = polarizedheader 4pin 0.156in [package=THT]

nets:
  N1: Raspberry_Pi_1.GND, H1.pin2
  N2: Raspberry_Pi_1.GPIO18, Power_plug1.GND, H1.pin4
  N3: Raspberry_Pi_1.GPIO15, H1.pin1
  N4: Power_plug1.VCC, H1.pin3

notes:
  12volt Supply
  12 volt PWM Fan with Tachometer
  PWM FAN
